# Fritzing sketch Impact Sensor (saved by Fritzing 1.0.1rc)

parts:
  Mod1 = Raspberry Pi Pico
  Part1 = Adafruit ADXL375 [part_number="Adafruit #5374"]
  microSD1 = MicroSD Card Module
  LED1 = smd LED [color="Red (633nm)" package="1206 [SMD]"]
  LED2 = smd LED [color="Red (633nm)" package="1206 [SMD]"]  # not connected
  LED3 = smd LED [color="Red (633nm)" package="1206 [SMD]"]  # not connected
  LED4 = smd LED [color="Red (633nm)" package="1206 [SMD]"]  # not connected
  LED5 = smd LED [color="Red (633nm)" package="1206 [SMD]"]  # not connected
  R5 = Resistor [tolerance=±5% resistance=220 package="1206 [SMD]"]  # not connected
  R4 = Resistor [tolerance=±5% resistance=220 package="1206 [SMD]"]  # not connected
  R3 = Resistor [tolerance=±5% resistance=220 package="1206 [SMD]"]  # not connected
  R2 = Resistor [tolerance=±5% resistance=220 package="1206 [SMD]"]  # not connected
  R1 = Resistor [tolerance=±5% resistance=220 package="1206 [SMD]"]  # not connected

nets:
  N1: Mod1.pin_1, microSD1.MISO
  N2: Mod1.pin_2, microSD1.CS
  N3: Mod1.pin_4, microSD1.SCK
  N4: Mod1.pin_5, microSD1.MOSI
  GND: Mod1.pin_23, Mod1.pin_28, Mod1.pin_38, Mod1.pin_42, Part1.GND, microSD1.GND, LED1.cathode
  N5: Mod1.pin_26, Part1.SDA/SDIO
  N6: Mod1.pin_27, Part1.SCL
  N7: Mod1.pin_36, Part1.VCC
  N8: Mod1.pin_40, microSD1.VCC

custom parts:
  Raspberry Pi Pico: Raspberry Pi Pico. Based around the RP2040 microcontroller the Pico is a low cost microcontroller device bringing Raspberry Pi quality, cost, and easy of use to the microcontroller space. Jan 2021, Split part in to two versions: tht (this one) and SMD. This one will drill holes for a .1 in header in pcb to allow plugging in the module as well as providing pads to solder the module to the top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
  Adafruit ADXL375: Hey rocket man (burnin' out your fuse out there alone) ever wonder how fast you're rocketing? The Adafruit ADXL375 High G Accelerometer is an epic +-200g 3-axis accelerometer may be able to tell the answer. You read that right, this accelerometer can sense up to 200 g's of force in three axes of measurements (X Y Z) has and pins that can be used either as I2C or SPI digital interfacing. for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
